# Fritzing sketch Meteo (saved by Fritzing 0.9.3b)
breadboards: 1

parts:
  Деталь1 = Arduino Uno (Rev3)
  LCD1 = LCD screen
  RHT1 = Humidity and Temperature Sensor RHT03
  R1 = Resistor [tolerance=±5% resistance=10k package=THT]
  S1 = Pushbutton [package="[THT]"]  # not connected
  Деталь2 = BME280 Breakout
  R2 = Resistor [tolerance=±5% resistance=3.3k package=THT]

nets:
  N1: Деталь1.A3, R2.Pin_0
  N2: Деталь1.A4/SDA, Деталь2.SDI/SDA
  N3: Деталь1.A5/SCL, Деталь2.SCK/SCL
  N4: Деталь1.D8, LCD1.E
  N5: Деталь1.D9_PWM, LCD1.DB4
  N6: Деталь1.D10_PWM/SS, LCD1.DB5
  N7: Деталь1.D11_PWM/MOSI, LCD1.DB6
  N8: Деталь1.D12/MISO, LCD1.DB7
  N9: Деталь1.D6_PWM, RHT1.Data-signal
  N10: Деталь1.D7, LCD1.RS
  3V3: Деталь1.3V3, Деталь2.3.3V
  5V: Деталь1.5V, LCD1.VDD, LCD1.V0, RHT1.Vcc
  GND: Деталь1.GND, LCD1.VSS, LCD1.R/W, LCD1.LED-, RHT1.GND_2, R1.Pin_1, Деталь2.GND
  N11: LCD1.LED+, R2.Pin_1
